# Fritzing sketch poe (saved by Fritzing 0.9.3b)
perfboards: 1

parts:
  Part1 = Arduino Uno (Rev3)  # not connected
  Part2 = Arduino Uno (Rev3)
  Part3 = Soil Moisture Sensor
  Part4 = Soil Moisture Sensor
  Part5 = Soil Moisture Sensor
  Part6 = Soil Moisture Sensor
  LED1 = RGB LED (6 legs) [package="5 mm [THT]"]  # not connected
  R1 = Resistor [tolerance=±5% resistance=536 package="0805 [SMD]"]  # not connected
  Part7 = Adafruit Motor/Stepper/Servo Shield [part_number="Adafruit #1438"]
  Part8 = Ambient Light Sensor (TEMT6000 Breakout Board)
  Part9 = Ambient Light Sensor (TEMT6000 Breakout Board)
  Part10 = Ambient Light Sensor (TEMT6000 Breakout Board)
  Part11 = Ambient Light Sensor (TEMT6000 Breakout Board)

nets:
  N1: Part2.A0, Part6.SIG
  N2: Part2.A1, Part5.SIG
  N3: Part2.A2, Part4.SIG
  N4: Part2.A3, Part3.SIG
  N5: Part2.A4/SDA, Part7.AD4/SDA
  N6: Part2.A5/SCL, Part7.AD5/SCL
  5V: Part2.5V, Part7.VIN
  GND: Part2.GND, Part7.GND
  N7: Part7.AD0, Part11.S
  N8: Part7.AD1, Part10.S
  N9: Part7.AD2, Part9.S
  N10: Part7.AD3, Part8.S

custom parts:
  Adafruit Motor/Stepper/Servo Shield: The original Adafruit Motorshield kit is one of our most beloved kits, which is why we decided to make something even better. We have upgraded the shield kit to make the bestest, easiest way to drive DC and Stepper motors. This shield will make quick work of your next robotics project! We kept the ability to drive up to 4 DC motors or 2 stepper motors, but added many improvements: Instead of a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
